# Fritzing sketch GPS_clock (saved by Fritzing 0.9.3b)
breadboards: 1

parts:
  Part1 = Arduino Uno (Rev3)
  U1 = LCD-16X2 [package=lcd-16x2_nosilk]
  R1 = Trimmer Potentiometer [maximum_resistance=10kΩ package=THT]
  U2 = D2523T [package=em406]

nets:
  N1: Part1.D8, U1.DB7
  N2: Part1.D9_PWM, U1.DB6
  N3: Part1.D10_PWM/SS, U1.DB5
  N4: Part1.D11_PWM/MOSI, U1.DB4
  N5: Part1.D12/MISO, U1.E
  N6: Part1.D13/SCK, U1.RS
  GND: Part1.GND, U1.VSS, U1.R_W, R1.leg2, U2.GND
  N7: Part1.D3_PWM, U2.TX
  N8: Part1.D4, U2.RX
  5V: Part1.5V, U1.VDD, R1.leg1, U2.VIN
  N9: U1.VO, R1.wiper
