# Fritzing sketch GPS_clock_nano (saved by Fritzing 0.9.3b)
breadboards: 1

parts:
  Part1 = Arduino Nano (Rev3.0)
  LCD1 = LCD screen
  U1 = D2523T [package=em406]
  R1 = Trimmer Potentiometer [maximum_resistance=10kΩ package=THT]

nets:
  N1: Part1.D2, LCD1.RS
  N2: Part1.D3, LCD1.E
  N3: Part1.D6, LCD1.DB4
  N4: Part1.D7, LCD1.DB5
  N5: Part1.D8, LCD1.DB6
  N6: Part1.D9, LCD1.DB7
  N7: Part1.D12/MISO, U1.LED
  GND: Part1.GND, LCD1.VSS, U1.VBAT
  N8: LCD1.V0, R1.wiper
