# Fritzing sketch GSM (saved by Fritzing 0.9.3b)
breadboards: 1

parts:
  Part1 = Arduino Uno (Rev3)
  GSM_SIM_GPSR_SMS_SIM900_SIM1 = SIM800L [package=THT]
  Q1 = NPN-Transistor [package="TO92 [THT]"]
  BAT1 = BC9VPC [package=bc9vpc]
  R1 = Resistor [tolerance=±5% resistance=220 package="0603 [SMD]"]
  M1 = DC Motor
  D1 = Rectifier Diode [part_number=1N4001 package="300 mil [THT]"]
  C1 = Capacitor [package=cap-pth-small2]

nets:
  N1: Part1.D12/MISO, R1.Pin_1
  GND: Part1.GND, GSM_SIM_GPSR_SMS_SIM900_SIM1.GND
  N2: Part1.D3_PWM, GSM_SIM_GPSR_SMS_SIM900_SIM1.SIM_RXD
  N3: Part1.D4, GSM_SIM_GPSR_SMS_SIM900_SIM1.SIM_TXD
  5V: Part1.5V, GSM_SIM_GPSR_SMS_SIM900_SIM1.5V
  N4: Q1.E, BAT1.V-
  N5: Q1.B, R1.Pin_0
  N6: Q1.C, M1.pin_2, D1.cathode, C1.2
  N7: BAT1.V+, M1.pin_1, D1.anode, C1.1
