# Fritzing sketch medi_new (saved by Fritzing 0.9.3b)
circuit board: 11.534cm x 8.52226cm
breadboards: 1

parts:
  Part2 = NRF24L01+ Breakout Board
  Part1 = Arduino Nano (Rev3.0)
  LED1 = smd LED [color="Red (633nm)" package="0805 [SMD]"]
  LED2 = smd LED [color="Red (633nm)" package="0805 [SMD]"]
  LED3 = smd LED [color="Red (633nm)" package="0805 [SMD]"]
  LED4 = smd LED [color="Red (633nm)" package="0805 [SMD]"]
  LED5 = smd LED [color="Red (633nm)" package="0805 [SMD]"]
  R1 = Resistor [tolerance=±5% resistance=220 package="0805 [SMD]"]
  R2 = Resistor [tolerance=±5% resistance=220 package="0805 [SMD]"]
  R3 = Resistor [tolerance=±5% resistance=220 package="0805 [SMD]"]
  R4 = Resistor [tolerance=±5% resistance=220 package="0805 [SMD]"]
  R5 = Resistor [tolerance=±5% resistance=220 package="0805 [SMD]"]
  RE1 = Rotary Encoder [package=THT]
  VCC1 = Battery block 9V
  VCC2 = Battery block 9V
  R6 = Resistor [tolerance=±5% resistance=220 package="0805 [SMD]"]
  IC1 = Voltage Regulator [package=to220-igo]
  R7 = Resistor [tolerance=±5% resistance=220 package="0805 [SMD]"]
  D1 = Diode [package=diode-1n4001]
  C1 = Capacitor [package=cap-pth-small2]
  OMRON1 = OMRON PCB Power Relay – G5LE [part_number="G5LE-1\n" package=THT]
  D2 = Diode [package=diode-1n4001]
  U1 = TRANSISTOR_NPN_2 [package=to-92]

nets:
  GND: Part2.GND, Part1.GND, LED1.anode, LED2.anode, LED3.anode, LED4.anode, LED5.anode, RE1.EncoderPinC, VCC1.-, VCC2.-, IC1.GND, R7.Pin_0, OMRON1.B, D2.A, U1.E
  VCC: Part2.VCC, Part1.3V3
  N1: Part2.CE, Part1.D9
  N2: Part2.CS, Part1.D8
  N3: Part2.SCK, Part1.D10
  N4: Part2.MOSI, Part1.D11/MOSI
  N5: Part2.MISO, Part1.D12/MISO
  N6: Part1.D1/TX, RE1.EncoderPinB
  N7: Part1.D0/RX, RE1.EncoderPinA
  N8: Part1.D3, R4.Pin_0
  N9: Part1.D4, R3.Pin_0
  N10: Part1.D5, R2.Pin_0
  N11: Part1.D6, R1.Pin_0
  N12: Part1.D7, R5.Pin_0
  N13: Part1.VIN, IC1.OUT
  N14: Part1.A7, R6.Pin_1, R7.Pin_1
  N15: Part1.A6, U1.B
  N16: LED1.cathode, R5.Pin_1
  N17: LED2.cathode, R1.Pin_1
  N18: LED3.cathode, R2.Pin_1
  N19: LED4.cathode, R3.Pin_1
  N20: LED5.cathode, R4.Pin_1
  N21: VCC1.+, D1.A, C1.1
  N22: VCC2.+, R6.Pin_0, IC1.IN, OMRON1.COIL1
  N23: D1.C, C1.2, OMRON1.C
  N24: OMRON1.A, D2.C
