# Fritzing sketch meditab_assign - RX (saved by Fritzing 0.9.3b)
circuit board: 14.0729cm x 10.4633cm
breadboards: 1

parts:
  Part1 = Arduino Nano (Rev3.0)
  Part2 = NRF24L01+ Breakout Board
  BAT1 = BC9VPC [package=bc9vpc]
  D1 = Diode [package=diode-hv]
  J1 = Screw terminal - 2 pins [package=THT]
  C1 = Capacitor [package=cap-pth-small2]
  R7 = Resistor [tolerance=±5% resistance=220 package="0603 [SMD]"]
  R8 = Resistor [tolerance=±5% resistance=220 package="0603 [SMD]"]
  IC1 = Voltage Regulator [package=to-220-alt]
  RELAY1 = CAR RELAY [part_number=NVF4-2 package=THT]
  Q1 = NPN-Transistor [package="TO92 [THT]"]
  D2 = Diode [package=diode-hv]
  U4 = SUP500F [package=sup500f]
  DRV_1 = DRV 8825 Stepper Motor Carrier, High Current [part_number="DRV 8825"]
  M1 = Stepper Motor - Bipolar
  U5 = LCD-16X2 [package=lcd-8x2]
  DRV_2 = DRV 8825 Stepper Motor Carrier, High Current [part_number="DRV 8825"]
  DRV_3 = DRV 8825 Stepper Motor Carrier, High Current [part_number="DRV 8825"]
  DRV_4 = DRV 8825 Stepper Motor Carrier, High Current [part_number="DRV 8825"]
  M2 = Stepper Motor - Bipolar
  M3 = Stepper Motor - Bipolar
  M4 = Stepper Motor - Bipolar
  V1 = DC Power [voltage=5]
  R9 = TRIMPOT [package=trimpot-5mm]
  R10 = Resistor [tolerance=±5% resistance=220 package="0603 [SMD]"]

nets:
  N1: Part1.D1/TX, U4.RX-I
  N2: Part1.D0/RX, U4.TX-O
  GND: Part1.GND, Part2.GND, BAT1.V-, J1.pin2, R8.Pin_1, IC1.GND, RELAY1.30, D2.A, U4.GND, DRV_1.GROUND_ST/_MT, DRV_1.GROUND_LOG, U5.VSS, U5.R_W, DRV_2.GROUND_ST/_MT, DRV_2.GROUND_LOG, DRV_3.GROUND_ST/_MT, DRV_3.GROUND_LOG, DRV_4.GROUND_ST/_MT, DRV_4.GROUND_LOG, V1.V-, R9.CCW, R10.Pin_1
  N3: Part1.D2, DRV_4.ENABLE
  N4: Part1.D3, DRV_3.ENABLE
  N5: Part1.D4, DRV_2.ENABLE
  N6: Part1.D5, DRV_1.ENABLE
  N7: Part1.D6, DRV_1.DIRECTION, DRV_2.DIRECTION, DRV_3.DIRECTION, DRV_4.DIRECTION
  N8: Part1.D7, DRV_1.STEP, DRV_2.STEP, DRV_3.STEP, DRV_4.STEP
  N9: Part1.D8, Q1.B
  N10: Part1.D9, Part2.CE
  N11: Part1.D10, Part2.CS
  N12: Part1.D11/MOSI, Part2.MISO
  N13: Part1.D12/MISO, Part2.MOSI
  N14: Part1.VIN, IC1.OUT
  5V: Part1.5V, Q1.C, U5.VDD, U5.A, R9.CW
  N15: Part1.A6, U5.DB7
  N16: Part1.A5, U5.DB6
  N17: Part1.A4, U5.DB5
  N18: Part1.A3, U5.DB4
  N19: Part1.A2, U5.E
  N20: Part1.A1, U5.RS
  N21: Part1.A0, R7.Pin_1, R8.Pin_0
  3V3: Part1.3V3, Part2.VCC
  N22: Part1.D13/SCK, Part2.SCK
  N23: BAT1.V+, IC1.IN
  N24: D1.A, J1.pin1, C1.1
  N25: D1.C, C1.2
  N26: R7.Pin_0, RELAY1.85
  N27: RELAY1.86, Q1.E, D2.C
  N28: DRV_1.VOLTAGE_ST/_MT, DRV_2.VOLTAGE_ST/_MT, DRV_3.VOLTAGE_ST/_MT, DRV_4.VOLTAGE_ST/_MT, V1.V+
  N29: DRV_1.OUT_2B, M1.A
  N30: DRV_1.OUT_2A, M1.C
  N31: DRV_1.OUT_1A, M1.B
  N32: DRV_1.OUT_1B, M1.D
  N33: U5.VO, R9.WIPER
  N34: U5.K, R10.Pin_0
  N35: DRV_2.OUT_2B, M2.A
  N36: DRV_2.OUT_2A, M2.C
  N37: DRV_2.OUT_1A, M2.B
  N38: DRV_2.OUT_1B, M2.D
  N39: DRV_3.OUT_2B, M3.A
  N40: DRV_3.OUT_2A, M3.C
  N41: DRV_3.OUT_1A, M3.B
  N42: DRV_3.OUT_1B, M3.D
  N43: DRV_4.OUT_2B, M4.A
  N44: DRV_4.OUT_2A, M4.C
  N45: DRV_4.OUT_1A, M4.B
  N46: DRV_4.OUT_1B, M4.D
