# Fritzing sketch meditab_assign (saved by Fritzing 0.9.3b)
circuit board: 14.0729cm x 10.4633cm
breadboards: 1

parts:
  Part1 = Arduino Nano (Rev3.0)
  RE1 = Rotary Encoder [package=THT]
  Part2 = NRF24L01+ Breakout Board
  BAT1 = BC9VPC [package=bc9vpc]
  D1 = Diode [package=diode-hv]
  J1 = Screw terminal - 2 pins [package=THT]
  C1 = Capacitor [package=cap-pth-small2]
  R7 = Resistor [tolerance=±5% resistance=220 package="0603 [SMD]"]
  R8 = Resistor [tolerance=±5% resistance=220 package="0603 [SMD]"]
  IC1 = Voltage Regulator [package=to-220-alt]
  RELAY1 = CAR RELAY [part_number=NVF4-2 package=THT]
  Q1 = NPN-Transistor [package="TO92 [THT]"]
  D2 = Diode [package=diode-hv]
  U1 = SUP500F [package=sup500f]
  U2 = LCD-16X2 [package=lcd-16x2]
  R9 = TRIMPOT [package=trimpot-5mm]
  R10 = Resistor [tolerance=±5% resistance=220 package=THT]
  S1 = Round Pushbutton
  S2 = Round Pushbutton
  S3 = Round Pushbutton
  S4 = Round Pushbutton

nets:
  N1: Part1.D1/TX, RE1.EncoderPinB
  N2: Part1.D0/RX, RE1.EncoderPinA
  GND: Part1.GND, RE1.EncoderPinC, Part2.GND, BAT1.V-, R8.Pin_1, IC1.GND, U1.GND, U2.VSS, U2.R_W, U2.K, R9.CW, S1.leg1, S2.leg1, S3.leg1, S4.leg1
  N3: Part1.D2, U2.DB7
  N4: Part1.D3, U2.DB6
  N5: Part1.D4, U2.DB5
  N6: Part1.D5, U2.DB4
  N7: Part1.D6, U2.E
  N8: Part1.D7, U2.RS
  N9: Part1.D8, Q1.B
  N10: Part1.D9, Part2.CE
  N11: Part1.D10, Part2.CS
  N12: Part1.D11/MOSI, Part2.MISO
  N13: Part1.D12/MISO, Part2.MOSI
  N14: Part1.VIN, IC1.OUT
  5V: Part1.5V, Q1.C, U2.VDD, R9.CCW, R10.Pin_1
  N15: Part1.A6, S4.leg0
  N16: Part1.A5, S3.leg0
  N17: Part1.A4, S2.leg0
  N18: Part1.A3, S1.leg0
  N19: Part1.A2, U1.RX-I
  N20: Part1.A1, U1.TX-O
  N21: Part1.A0, R7.Pin_1, R8.Pin_0
  VCC: Part1.3V3, Part2.VCC, U1.VCC
  N22: Part1.D13/SCK, Part2.SCK
  N23: BAT1.V+, IC1.IN
  N24: D1.A, J1.pin1, C1.1
  N25: D1.C, C1.2, RELAY1.87A
  N26: J1.pin2, RELAY1.30, D2.A
  N27: R7.Pin_0, RELAY1.85
  N28: RELAY1.86, Q1.E, D2.C
  N29: U2.VO, R9.WIPER
  N30: U2.A, R10.Pin_0
